// Digital circuit CerrojoD(ultimo).dig as structural Verilog
module CerrojoD_ultimo (
  input  D,
  input  CLK,
  output Q,
  output Q_2
);

  wire nand_1_out, nand_2_out, not_1_out;

  not not_1 (not_1_out, D);
  nand nand_1 (nand_1_out, D, CLK);
  nand nand_2 (nand_2_out, not_1_out, CLK);
  nand nand_3 (Q, nand_1_out, Q_2);
  nand nand_4 (Q_2, Q, nand_2_out);

  // Notes on the sheet:
  //   CLK: default 1
endmodule
