// Digital circuit FlipFlopD.dig as structural Verilog
module FlipFlopD (
  input  CLK,
  input  D,
  output Q
);

  wire cerrojod_1_q, not_1_out;

  not not_1 (not_1_out, CLK);
  CerrojoD cerrojod_1 (.D(D), .CLK(CLK), .Q(cerrojod_1_q));  // open: Q_2
  CerrojoD cerrojod_2 (.D(cerrojod_1_q), .CLK(not_1_out), .Q(Q));  // open: Q_2
endmodule
