// Digital circuit Semaforo.dig as structural Verilog
module Semaforo (
  input  P,
  input  CLK
);

  wire and_1_out, and_2_out, and_3_out, and_4_out, and_5_out, and_6_out, D0_q, D1_q, not_1_out, not_2_out,
       not_3_out, or_1_out, xor_1_out;

  not not_1 (not_1_out, D0_q);
  and and_1 (and_1_out, not_1_out, D1_q);
  and and_2 (and_2_out, not_1_out, P);
  xor xor_1 (xor_1_out, D1_q, D0_q);
  or or_1 (or_1_out, and_1_out, and_2_out);
  FlipFlopD D1 (.CLK(CLK), .D(xor_1_out), .Q(D1_q));
  FlipFlopD D0 (.CLK(CLK), .D(or_1_out), .Q(D0_q));
  not not_2 (not_2_out, D1_q);
  not not_3 (not_3_out, D0_q);
  and and_3 (and_3_out, not_2_out, D0_q);
  and and_4 (and_4_out, not_2_out, not_3_out);
  and and_5 (and_5_out, D1_q, D0_q);
  and and_6 (and_6_out, D1_q, not_3_out);
  LED LP2 (.in(D1_q));
  LED LP1 (.in(and_3_out));
  LED LP0 (.in(and_4_out));
  LED LS2 (.in(not_2_out));
  LED LS1 (.in(and_5_out));
  LED LS0 (.in(and_6_out));
endmodule
